# Fritzing sketch diagram (saved by Fritzing 0.7.4b)
breadboards: 2

parts:
  R1 = 100 Ω Resistor [package=THT]
  Arduino1 = Arduino
  R2 = 100 Ω Resistor [package=THT]
  LED3 = LED - 5mm [color="Red (633nm)" package="5 mm [THT]"]
  R3 = 100 Ω Resistor [package=THT]
  J1 = Basic Servo
  S1 = Round Pushbutton
  S2 = Round Pushbutton
  J2 = Basic Servo
  J3 = Basic Servo
  S3 = Reed switch [package=THT]
  J4 = Infrared Proximity Sensor
  LED4 = LED - 5mm [color="Red (633nm)" package="5 mm [THT]"]
  LED5 = LED - 5mm [color="Red (633nm)" package="5 mm [THT]"]

nets:
  N1: R1.Pin_0, LED5.anode
  GND: Arduino1.GND, LED3.cathode, S1.leg0, S2.leg0, J3.gnd, S3.pin_3, J4.GND, LED4.cathode, LED5.cathode
  N2: Arduino1.D12, S3.pin_1
  N3: Arduino1.D11, J1.pulse
  N4: Arduino1.D10, J2.pulse
  N5: Arduino1.D9, J3.pulse
  N6: Arduino1.D6, R3.Pin_1
  N7: Arduino1.D5, S1.leg1
  N8: Arduino1.D4, S2.leg1
  N9: Arduino1.D3, J4.echo
  N10: Arduino1.D2, J4.trigger
  VCC: Arduino1.+5V, J3.vcc, J4.Vcc
  N11: R2.Pin_0, LED4.anode
  N12: LED3.anode, R3.Pin_0

notes:
  out of range
  in range
  override
  distance sensor
  manual override
  return to automatic mode
  fan relay
  A/V receiver servo
  Treadmill STOP button servo
  Treadmill START button servo

custom parts:
  100 Ω Resistor: A generic resistor (0.25W)
